// Logisim project Cravo_project.circ as structural Verilog: 8 circuits, main circuit ADD_4
module ADD_4 (
  input  [3:0] B,
  input  [3:0] A,
  input  CarryIN,
  output CarryOUT,
  output [3:0] S
);

  wire add_1_2_carryout, add_1_3_carryout, add_1_4_carryout;

  ADD_1 add_1_1 (.A(A[3]), .B(B[3]), .CarryIN(add_1_2_carryout), .S(S[3]), .CarryOUT(CarryOUT));
  ADD_1 add_1_2 (.A(A[2]), .B(B[2]), .CarryIN(add_1_3_carryout), .S(S[2]), .CarryOUT(add_1_2_carryout));
  ADD_1 add_1_3 (.A(A[1]), .B(B[1]), .CarryIN(add_1_4_carryout), .S(S[1]), .CarryOUT(add_1_3_carryout));
  ADD_1 add_1_4 (.A(A[0]), .B(B[0]), .CarryIN(CarryIN), .S(S[0]), .CarryOUT(add_1_4_carryout));
endmodule

module ADD_1 (
  input  A,
  input  B,
  input  CarryIN,
  output S,
  output CarryOUT
);

  wire and_1_out, and_2_out, or_1_out, xor_1_out;

  xor xor_1 (xor_1_out, A, B);
  or or_1 (or_1_out, CarryIN, B);
  and and_1 (and_1_out, CarryIN, B);
  LED led_1 (.in(S));
  xor xor_2 (S, xor_1_out, CarryIN);
  and and_2 (and_2_out, or_1_out, A);
  LED led_2 (.in(CarryOUT));
  or or_2 (CarryOUT, and_2_out, and_1_out);
endmodule

module Main (
  input  [3:0] A,
  input  [3:0] B,
  input  [2:0] \Operações ,
  output out_4,
  output out_5,
  output [3:0] S
);

  wire decod_3x8_1_s0, decod_3x8_1_s1, decod_3x8_1_s2, decod_3x8_1_s4;
  wire [3:0] add_4_1_s, sub_4_1_s;

  BUF buf_1 (.B(B), .in_2(decod_3x8_1_s0), .S(S));
  DECOD_3X8 decod_3x8_1 (
    .OP(\Operações ), .S0(decod_3x8_1_s0), .S1(decod_3x8_1_s1), .S2(decod_3x8_1_s2), .S4(decod_3x8_1_s4));  // open: S3, S5, S6, S7
  ADD_4 add_4_1 (.CarryOUT(out_4), .CarryIN(1'b0), .S(add_4_1_s), .A(A), .B(B));
  BUF buf_2 (.B(add_4_1_s), .in_2(decod_3x8_1_s1), .S(S));
  SUB_4 sub_4_1 (.B(B), .A(A), .CarryOUT(out_5), .CarryIN(1'b0), .S(sub_4_1_s));
  BUF buf_3 (.B(sub_4_1_s), .in_2(decod_3x8_1_s2), .S(S));
  DEBUF debuf_1 (.B(B), .in_2(decod_3x8_1_s4), .S(S));
endmodule

module SUB_1 (
  input  A,
  input  B,
  input  CarryIN,
  output S,
  output CarryOUT
);

  wire and_1_out, and_2_out, or_1_out, xor_1_out;

  xor xor_1 (xor_1_out, A, B);
  or or_1 (or_1_out, CarryIN, B);
  and and_1 (and_1_out, or_1_out, ~A);  // AND_Gate
  and and_2 (and_2_out, CarryIN, B);
  LED led_1 (.in(S));
  xor xor_2 (S, xor_1_out, CarryIN);
  LED led_2 (.in(CarryOUT));
  or or_2 (CarryOUT, and_1_out, and_2_out);
endmodule

module SUB_4 (
  input  [3:0] B,
  input  [3:0] A,
  input  CarryIN,
  output CarryOUT,
  output [3:0] S
);

  wire sub_1_2_carryout, sub_1_3_carryout, sub_1_4_carryout;

  SUB_1 sub_1_1 (.A(A[3]), .B(B[3]), .CarryIN(sub_1_2_carryout), .S(S[3]), .CarryOUT(CarryOUT));
  SUB_1 sub_1_2 (.A(A[2]), .B(B[2]), .CarryIN(sub_1_3_carryout), .S(S[2]), .CarryOUT(sub_1_2_carryout));
  SUB_1 sub_1_3 (.A(A[1]), .B(B[1]), .CarryIN(sub_1_4_carryout), .S(S[1]), .CarryOUT(sub_1_3_carryout));
  SUB_1 sub_1_4 (.A(A[0]), .B(B[0]), .CarryIN(CarryIN), .S(S[0]), .CarryOUT(sub_1_4_carryout));
endmodule

module BUF (
  input  [3:0] B,
  input  in_2,
  output [3:0] S
);

  assign S[1] = in_2 ? B[1] : 1'bz;  // Controlled_Buffer controlled_buffer_1
  assign S[3] = in_2 ? B[3] : 1'bz;  // Controlled_Buffer controlled_buffer_2
  assign S[2] = in_2 ? B[2] : 1'bz;  // Controlled_Buffer controlled_buffer_3
  assign S[0] = in_2 ? B[0] : 1'bz;  // Controlled_Buffer controlled_buffer_4
endmodule

module DEBUF (
  input  [3:0] B,
  input  in_2,
  output [3:0] S
);

  assign S[1] = in_2 ? ~B[1] : 1'bz;  // Controlled_Inverter controlled_inverter_1
  assign S[3] = in_2 ? ~B[3] : 1'bz;  // Controlled_Inverter controlled_inverter_2
  assign S[2] = in_2 ? ~B[2] : 1'bz;  // Controlled_Inverter controlled_inverter_3
  assign S[0] = in_2 ? ~B[0] : 1'bz;  // Controlled_Inverter controlled_inverter_4
endmodule

module DECOD_3X8 (
  input  [2:0] OP,
  output S0,
  output S1,
  output S2,
  output S3,
  output S4,
  output S5,
  output S6,
  output S7
);

  and and_1 (S0, ~OP[2], ~OP[1], ~OP[0]);  // AND_Gate
  and and_2 (S1, ~OP[2], ~OP[1], OP[0]);  // AND_Gate
  and and_3 (S2, ~OP[2], OP[1], ~OP[0]);  // AND_Gate
  and and_4 (S3, ~OP[2], OP[1], OP[0]);  // AND_Gate
  and and_5 (S4, OP[2], ~OP[1], ~OP[0]);  // AND_Gate
  and and_6 (S5, OP[2], ~OP[1], OP[0]);  // AND_Gate
  and and_7 (S6, OP[2], OP[1], ~OP[0]);  // AND_Gate
  and and_8 (S7, OP[2], OP[1], OP[0]);
endmodule
